// Logisim project aoc786201-lab05.circ as structural Verilog: 6 circuits, main circuit Registrador
module Registrador (
  input  [3:0] D,
  input  LOAD,
  input  CLR
);

  wire clock_1_out;
  wire [3:0] register_1_q;

  Clock clock_1 (.out(clock_1_out));
  Hex_Digit_Display hex_digit_display_1 (.value(register_1_q));  // open: dp
  Register #(.width(4)) register_1 (.D(D), .en(LOAD), .Q(register_1_q), .clk(clock_1_out), .clr(CLR));
endmodule

module Contador (
);

  wire adder_1_cout, clock_1_out;
  wire [3:0] adder_1_out, register_1_q;

  Clock clock_1 (.out(clock_1_out));
  Register #(.width(4)) register_1 (.D(adder_1_out), .Q(register_1_q), .clk(clock_1_out));  // open: en, clr
  Adder #(.width(4)) adder_1 (.a(4'b0001), .b(register_1_q), .out(adder_1_out), .cout(adder_1_cout));  // open: cin
  LED led_1 (.in(adder_1_cout));
  Hex_Digit_Display hex_digit_display_1 (.value(register_1_q));  // open: dp
endmodule

module PC (
  input  [3:0] DESTINO,
  input  LOAD,
  input  CLR
);

  wire clock_1_out, not_1_out;
  wire [3:0] counter_1_q;

  Clock clock_1 (.out(clock_1_out));
  not not_1 (not_1_out, LOAD);
  Counter #(.width(4), .max('hf)) counter_1 (
    .load(LOAD), .D(DESTINO), .count(not_1_out), .Q(counter_1_q), .clk(clock_1_out), .clr(CLR));  // open: carry
  Hex_Digit_Display hex_digit_display_1 (.value(counter_1_q));  // open: dp
endmodule

module Memoria (
  input  [1:0] A,
  input  [3:0] DIN,
  input  WE
);

  wire clock_1_out;
  wire [3:0] ram_1_data;

  Clock clock_1 (.out(clock_1_out));
  RAM #(.addrWidth(2), .dataWidth(4), .bus("separate")) ram_1 (
    .addr(A), .din(DIN), .data(ram_1_data), .str(WE), .clk(clock_1_out));  // open: sel, ld, clr
  Hex_Digit_Display hex_digit_display_1 (.value(ram_1_data));  // open: dp
endmodule

module Semaforo (
);

  wire clock_1_out;
  wire [2:0] counter_1_q, rom_1_data;

  Clock clock_1 (.out(clock_1_out));
  Counter #(.width(3), .max('h7)) counter_1 (.Q(counter_1_q), .clk(clock_1_out));  // open: load, D, count, carry, clr
  ROM #(.addrWidth(3), .dataWidth(3)) rom_1 (.addr(counter_1_q), .data(rom_1_data));  // open: sel
  LED led_1 (.in(rom_1_data[0]));
  LED led_2 (.in(rom_1_data[1]));
  LED led_3 (.in(rom_1_data[2]));
endmodule

module Sequenciador (
  input  RST,
  input  CLK,
  output [3:0] PC,
  output [3:0] CMD,
  output [3:0] OPR
);

  Hex_Digit_Display hex_digit_display_1 (.value(PC));  // open: dp
  Counter #(.width(4), .max('hf)) u_PC (.Q(PC), .clk(CLK), .clr(RST));  // open: load, D, count, carry
  ROM #(.addrWidth(4)) rom_1 (.addr(PC), .data({OPR, CMD}));  // open: sel
  Hex_Digit_Display hex_digit_display_2 (.value(OPR));  // open: dp
  Hex_Digit_Display hex_digit_display_3 (.value(CMD));  // open: dp
endmodule
